# Fritzing sketch nerf-turret (saved by Fritzing 0.9.4)
circuit board: 8.5cm x 5.65cm
breadboards: 1

parts:
  Horizontal = Pololu A4988 [package=SO16]
  Vertical = Pololu A4988 [package=SO16]
  12V_IN = Camdenboss CTB0158-2 [part_number=CTB0158-2 package=THT]
  C1 = Capacitor Polarized [package=cpol-radial-10uf-25v]
  12V_USB = Camdenboss CTB0158-2 [part_number=CTB0158-2 package=THT]
  C2 = Capacitor Polarized [package=cpol-radial-10uf-25v]
  RasPi_1 = male pin header, 20 pins [form="♂ (male)"]
  Hor_M = male pin header, 4 pins [form="♂ (male)"]
  Ver_M = male pin header, 4 pins [form="♂ (male)"]
  Rot_Ctrl = Camdenboss CTB0158-3 [part_number=CTB0158-3 package=THT]
  Tri_Rel = Camdenboss CTB0158-2 [part_number=CTB0158-2 package=THT]
  Tri_Ctrl = Camdenboss CTB0158-3 [part_number=CTB0158-3 package=THT]
  Rot_Rel = Camdenboss CTB0158-2 [part_number=CTB0158-2 package=THT]
  Tri_M = Camdenboss CTB0158-2 [part_number=CTB0158-2 package=THT]
  Rot_M = Camdenboss CTB0158-2 [part_number=CTB0158-2 package=THT]
  Trigger_D1 = Rectifier Diode [part_number=1N4001 package="300 mil [THT]"]

nets:
  VDD: Horizontal.MS1, Horizontal.MS2, Horizontal.VDD, Vertical.MS1, Vertical.MS2, Vertical.VDD, RasPi_1.pin1, Tri_Ctrl.pin1
  GND: Horizontal.MS3, Horizontal.GND, Vertical.MS3, Vertical.GND, 12V_IN.pin2, C1.-, 12V_USB.pin2, C2.-, RasPi_1.pin3, Rot_Ctrl.pin2, Tri_Ctrl.pin2, Tri_M.pin2, Rot_M.pin2, Trigger_D1.anode
  N1: Horizontal.RESET, Horizontal.SLEEP
  N2: Horizontal.STEP, RasPi_1.pin6
  N3: Horizontal.DIR, RasPi_1.pin8
  N4: Horizontal.1B, Hor_M.pin4
  N5: Horizontal.1A, Hor_M.pin3
  N6: Horizontal.2A, Hor_M.pin2
  N7: Horizontal.2B, Hor_M.pin1
  N8: Horizontal.VMOT, Vertical.VMOT, 12V_IN.pin1, C1.+, 12V_USB.pin1, C2.+, Tri_Rel.pin1, Rot_Rel.pin1
  N9: Vertical.RESET, Vertical.SLEEP
  N10: Vertical.STEP, RasPi_1.pin9
  N11: Vertical.DIR, RasPi_1.pin11
  N12: Vertical.1B, Ver_M.pin4
  N13: Vertical.1A, Ver_M.pin3
  N14: Vertical.2A, Ver_M.pin2
  N15: Vertical.2B, Ver_M.pin1
  N16: RasPi_1.pin12, Tri_Ctrl.pin3
  N17: RasPi_1.pin13, Rot_Ctrl.pin3
  N18: Tri_Rel.pin2, Tri_M.pin1, Trigger_D1.cathode
  N19: Rot_Rel.pin2, Rot_M.pin1

notes:
  andreas@granig.com
  Nerf Turret v1.0
